# Fritzing sketch ESP32 (saved by Fritzing 0.9.3b)
circuit board: 8.46667cm x 5.64444cm

parts:
  CODE_CANVAS = MH-ET LIVE ESP32 DEVKIT 38 pins
  A1 = w5500 module
  J1 = female pin header, 19 pins [form="♀ (female)"]
  J2 = female pin header, 19 pins [form="♀ (female)"]
  PWR2 = Header 3 [package=jst-3-pth]  # not connected
  PWR3 = Header 4 [package=jst-4-pth]  # not connected
  PWR1 = Header 2 [package=jst-2-pth]  # not connected
  PWR = Header 2 [package=jst-2-pth]
  U2 = Molex Picoblade Series Header [part_number=0533980371 package=Picoblade-53398-0371]  # not connected
  U1 = Molex Picoblade Series Header [part_number=0533980271 package=Picoblade-53398-0271]  # not connected
  U3 = Molex Picoblade Series Header [part_number=0532610719 package=Picoblade-53261-0719]  # not connected
  JP1 = Header 3 [package=jst-3-pth]  # not connected
  J3 = female pin header, 2 pins [form="♀ (female)"]  # not connected

nets:
  N1: CODE_CANVAS.3V3, A1.Pin_10, A1.Pin_11, J1.pin19
  N2: CODE_CANVAS.GND, A1.Pin_1, A1.Pin_12, J2.pin19
  N3: CODE_CANVAS.IO23, A1.Pin_3, J2.pin18
  N4: CODE_CANVAS.IO19, A1.Pin_7, J2.pin12
  N5: CODE_CANVAS.IO18, A1.Pin_4, J2.pin11
  N6: CODE_CANVAS.IO5, A1.Pin_5, J2.pin10
  N7: J1.pin1, PWR.2
  N8: J1.pin6, PWR.1

custom parts:
  MH-ET LIVE ESP32 DEVKIT 38 pins: http://mh.nodebb.com/topic/2/mh-et-live-esp32-devkit
  w5500 module: MELIFE 3pcs W5500 SPI to LAN Ethernet Network Module TCP IP STM32 Interface 3.3V 5V Compatible with WIZ820io RC5.
